# Fritzing sketch Esquematico_Tesis (saved by Fritzing 1.0.5)

parts:
  A1 = ESP32 DevKitc V4
  Part1 = InvenSense MPU6050
  M3 = MDD10A  # not connected
  BAT1 = Lithium Ion Polymer Battery 11.1v 5000mah  # not connected
  M4 = RioRand LM2596  # not connected
  CUI-enc1 = AMT103  # not connected
  M2 = DC Motor [voltage_(max)=6V voltage_(min)=3V]  # not connected
  M1 = DC Motor [voltage_(max)=6V voltage_(min)=3V]  # not connected
  CUI-enc2 = AMT103  # not connected
  microSD1 = MicroSD Card Module  # not connected

nets:
  N1: A1.Pin_1, Part1.VCC
  N2: A1.Pin_38, Part1.GND

notes:
  Encoders
  IMU
  MicroSD
  ESP32
  Bateria LiPo 11.1V
  Regulador de Voltaje
  Puente H
  Motores DC

custom parts:
  ESP32 DevKitc V4: ESP32-DevKitC board with ESP32-WROOM-32 module. ESP32-DevKitC V4 is a small-sized ESP32-based development board produced by Espressif. Most of the pins on the ESP module are broken out to the pin headers on the board. The pins D0, D1, D2, D3, CMD and CLK are used internally for communication between ESP32 and SPI flash memory. They are grouped on both sides near the USB connector. Avoid using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
